// Logisim project control-logic.circ as structural Verilog: 1 circuit, main circuit control_logic
module control_logic (
  input  [31:0] Instruction,
  input  BrEq,
  input  BrLt,
  output PCSel,
  output RegWEn,
  output [2:0] ImmSel,
  output BrUn,
  output ASel,
  output BSel,
  output [3:0] ALUSel,
  output MemWEn,
  output [1:0] WBSel
);

  wire comparator_1_eq, comparator_2_eq, comparator_3_eq, comparator_4_eq, comparator_5_eq, comparator_6_eq,
       demultiplexer_1_out0, demultiplexer_1_out1, priority_encoder_1_p1;
  wire [5:0] priority_encoder_1_p2;
  wire [15:14] rom_1_data;

  ROM #(.addrWidth(6), .dataWidth(16)) rom_1 (
    .addr(priority_encoder_1_p2), .data({rom_1_data, WBSel, MemWEn, ALUSel, BSel, ASel, BrUn, ImmSel, RegWEn}));
  // Priority_Encoder #(.select_enc(6)) priority_encoder_1: pin names not known; wires that end beside it: priority_encoder_1_p1, priority_encoder_1_p2
  Comparator #(.mode("unsigned"), .width(10)) comparator_1 (
    .a(10'h13), .b({Instruction[14:12], Instruction[6:0]}), .eq(comparator_1_eq));  // open: gt, lt
  Comparator #(.mode("unsigned"), .width(10)) comparator_2 (
    .a(10'h93), .b({Instruction[14:12], Instruction[6:0]}), .eq(comparator_2_eq));  // open: gt, lt
  Comparator #(.mode("unsigned"), .width(10)) comparator_3 (
    .a(10'h113), .b({Instruction[14:12], Instruction[6:0]}), .eq(comparator_3_eq));  // open: gt, lt
  Comparator #(.mode("unsigned"), .width(10)) comparator_4 (
    .a(10'h213), .b({Instruction[14:12], Instruction[6:0]}), .eq(comparator_4_eq));  // open: gt, lt
  Demultiplexer demultiplexer_1 (
    .out0(demultiplexer_1_out0), .out1(demultiplexer_1_out1), .in(comparator_5_eq), .sel(Instruction[30]));
  Comparator #(.mode("unsigned"), .width(10)) comparator_5 (
    .a(10'h293), .b({Instruction[14:12], Instruction[6:0]}), .eq(comparator_5_eq));  // open: gt, lt
  Comparator #(.mode("unsigned"), .width(10)) comparator_6 (
    .a(10'h313), .b({Instruction[14:12], Instruction[6:0]}), .eq(comparator_6_eq));  // open: gt, lt
  Comparator #(.mode("unsigned"), .width(10)) comparator_7 (
    .a(10'h393), .b({Instruction[14:12], Instruction[6:0]}), .eq(priority_encoder_1_p1));  // open: gt, lt

  assign PCSel = 1'b0;

  // Other names for the same wires on the sheet: funct7[2:0] = Instruction[31:29]

  // Notes on the sheet:
  //   INPUTS to your circuit
  //   Connect ROM Input here ->
  //   contents of rom_1 (hex, n*v repeats v):
  //   1041 10c1 1141 1241 12c1 16c1 1341 13c1
  //   ROM FOR CONTROL LOGIC
  //   DON'T CHANGE THE LOCATIONS OF THE INPUTS AND OUTPUTS!
  //   This is only if you choose to do the ROM option
  //   OUTPUT from your circuit
  //   Reminder: If using ROM, use combinational logic for PCSel
endmodule
